# Fritzing sketch FRIT (saved by Fritzing 0.9.9b)

parts:
  L298N1 = L298N DC motor driver
  Part1 = Arduino Uno (Rev3)
  M1 = gear-motor
  M2 = gear-motor
  VCC1 = Battery block 9V
  SEN1 = US-100 Ultrasonic Distance Sensor

nets:
  N1: L298N1.OUT1, M1.pin_1
  N2: L298N1.OUT2, M1.pin_2
  N3: L298N1.OUT3, M2.pin_2
  N4: L298N1.OUT4, M2.pin_1
  N5: L298N1.12V, VCC1.+
  GND: L298N1.GND, Part1.GND, VCC1.-, SEN1.GND, SEN1.GND-2
  5V: L298N1.5V, Part1.VIN
  N6: L298N1.IN1, Part1.D2
  N7: L298N1.IN2, Part1.D3_PWM
  N8: L298N1.IN3, Part1.D4
  N9: L298N1.IN4, Part1.D5_PWM
  N10: Part1.A0, SEN1.TRIG
  N11: Part1.A1, SEN1.ECHO
  3V3: Part1.3V3, SEN1.VCC

custom parts:
  L298N DC motor driver: 2x DC motor driver with 78M05 positive voltage regulator (7..35 V) L298N: max 46 V, 2 A Set 5 V Enable jumper to enable 5 V regultor (needed for the L298N) and +5 V output at screw terminal or supply external +5 V at screw terminal Set ENA and/or ENB to +5 V to enable motor permanently or supply ENA and/or ENB with PWM signal IN1 and IN2 set rotation directory for motor A (OUT1/OUT2) IN2 and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
